# Fritzing sketch metrônomo_severo (saved by Fritzing 0.9.4)
circuit board: 8.34085cm x 11.1592cm
breadboards: 1

parts:
  Componente1 = Arduino Uno (Rev3)
  R1 = Resistor [tolerance=±5% resistance=150 power=1 package=THT]
  R2 = Resistor [tolerance=±5% resistance=150 package=THT]
  R3 = Resistor [tolerance=±5% resistance=150 package=THT]
  R4 = Resistor [tolerance=±5% resistance=150 package=THT]
  LED1 = LED - 5mm [color="Red (633nm)" package="5 mm [THT]"]
  LED2 = LED - 5mm [color="Red (633nm)" package="5 mm [THT]"]
  LED4 = LED - 5mm [color="Red (633nm)" package="5 mm [THT]"]
  Q1 = MOSFET-NCHANNEL [package=to-92]
  Power_plug1 = Power plug
  Q2 = MOSFET-NCHANNEL [package=to-92]
  D2 = Zener Diode [part_number=1N4732A breakdown_voltage=3.6V package="300 mil [THT]"]
  R6 = Resistor [tolerance=±5% resistance=220 package=THT]
  Q3 = MOSFET-NCHANNEL [package=to-92]
  D3 = Zener Diode [part_number=1N4732A breakdown_voltage=3.6V package="300 mil [THT]"]
  R7 = Resistor [tolerance=±5% resistance=220 package=THT]
  Q4 = MOSFET-NCHANNEL [package=to-92]
  D4 = Zener Diode [part_number=1N4732A breakdown_voltage=3.6V package="300 mil [THT]"]
  R8 = Resistor [tolerance=±5% resistance=220 package=THT]
  Q5 = MOSFET-NCHANNEL [package=to-92]
  D5 = Zener Diode [part_number=1N4732A breakdown_voltage=3.6V package="300 mil [THT]"]
  R9 = Resistor [tolerance=±5% resistance=220 package=THT]
  LED3 = LED - 5mm [color="Red (633nm)" package="5 mm [THT]"]
  D1 = Zener Diode [part_number=1N4732A breakdown_voltage=12.1V package="300 mil [THT]"]
  R5 = Resistor [tolerance=±5% resistance=220 package=THT]
  J1 = double row male pin header, 2 pins [form="♂ (male)"]
  J2 = double row male pin header, 2 pins [form="♂ (male)"]
  J3 = double row male pin header, 2 pins [form="♂ (male)"]
  J4 = double row male pin header, 2 pins [form="♂ (male)"]

nets:
  N1: Componente1.D8, R8.Pin_1, J2.pin1
  N2: Componente1.D12/MISO, R7.Pin_1, J3.pin1
  N3: Componente1.D13/SCK, R6.Pin_1, J4.pin1
  GND: Componente1.GND, Q1.S, Power_plug1.GND
  N4: Componente1.D2, R9.Pin_1, J1.pin1
  N5: Componente1.D3_PWM, R5.Pin_1
  5V: Componente1.5V
  12V: Componente1.VIN, Power_plug1.VCC, Q2.D, D2.cathode, Q3.D, D3.cathode, Q4.D, D4.cathode, Q5.D, D5.cathode, D1.cathode
  N6: R1.Pin_0, R2.Pin_0, R3.Pin_0, R4.Pin_0, Q1.D
  N7: R1.Pin_1, LED2.cathode
  N8: R2.Pin_1, LED1.cathode
  N9: R3.Pin_1, LED3.cathode
  N10: R4.Pin_1, LED4.cathode
  N11: LED2.anode, J2.pin2
  N12: LED4.anode, J4.pin2
  N13: Q1.G, D1.anode, R5.Pin_0
  N14: Q2.G, D2.anode, R6.Pin_0
  N15: Q3.G, D3.anode, R7.Pin_0
  N16: Q4.G, D4.anode, R8.Pin_0
  N17: Q5.S, J1.pin2
  N18: Q5.G, D5.anode, R9.Pin_0
  N19: LED3.anode, J3.pin2

notes:
  Metrônomo Severo!
  V1.5

custom parts:
  MOSFET-NCHANNEL: Generic NMOS footprint
